// Logisim project Trab5-Jordan.circ as structural Verilog
module Trab1 (
  input  [31:0] Read_Adress_In,
  input  WE,
  input  Clk,
  input  RESET,
  output [31:0] Read_Adress_Out,
  output [31:0] Instruction
);

  Register #(.width(32)) register_1 (.D(Read_Adress_In), .en(WE), .clk(Clk), .Q(Read_Adress_Out), .clr(RESET));
  ROM #(.addrWidth(24), .dataWidth(32)) rom_1 (.addr(Read_Adress_Out[25:2]), .data(Instruction));

  // Notes on the sheet:
  //   contents of rom_1 (hex, n*v repeats v):
  //   432020 432022 400008 8000001 5*0 c000003
endmodule

module Trab2_Registers (
  input  [4:0] READ_REGISTER_1,
  input  [4:0] READ_REGISTER_2,
  input  [4:0] WRITE_REGISTER,
  input  [31:0] WRITE_DATA,
  input  WRITE,
  input  CLOCK,
  output [31:0] READ_DATA_1,
  output [31:0] READ_DATA_2
);

  wire [7:0] demultiplexer_1_out0, demultiplexer_1_out8, demultiplexer_1_out16, demultiplexer_1_out24;
  wire [31:0] register_1_q, register_2_q, register_3_q, register_4_q, register_5_q, register_6_q,
       register_7_q, register_8_q, register_9_q, register_10_q, register_11_q, register_12_q, register_13_q,
       register_14_q, register_15_q, register_16_q, register_17_q, register_18_q, register_19_q,
       register_20_q, register_21_q, register_22_q, register_23_q, register_24_q, register_25_q,
       register_26_q, register_27_q, register_28_q, register_29_q, register_30_q, register_31_q,
       register_32_q;

  Demultiplexer #(.select(5), .enable("false")) demultiplexer_1 (
    .out0(demultiplexer_1_out0[0]), .out1(demultiplexer_1_out0[1]), .out2(demultiplexer_1_out0[2]),
    .out3(demultiplexer_1_out0[3]), .out4(demultiplexer_1_out0[4]), .out5(demultiplexer_1_out0[5]),
    .out6(demultiplexer_1_out0[6]), .out7(demultiplexer_1_out0[7]), .out8(demultiplexer_1_out8[0]),
    .out9(demultiplexer_1_out8[1]), .out10(demultiplexer_1_out8[2]), .out11(demultiplexer_1_out8[3]),
    .out12(demultiplexer_1_out8[4]), .out13(demultiplexer_1_out8[5]), .out14(demultiplexer_1_out8[6]),
    .out15(demultiplexer_1_out8[7]), .out16(demultiplexer_1_out16[0]), .out17(demultiplexer_1_out16[1]),
    .out18(demultiplexer_1_out16[2]), .out19(demultiplexer_1_out16[3]), .out20(demultiplexer_1_out16[4]),
    .out21(demultiplexer_1_out16[5]), .out22(demultiplexer_1_out16[6]), .out23(demultiplexer_1_out16[7]),
    .out24(demultiplexer_1_out24[0]), .out25(demultiplexer_1_out24[1]), .out26(demultiplexer_1_out24[2]),
    .out27(demultiplexer_1_out24[3]), .out28(demultiplexer_1_out24[4]), .out29(demultiplexer_1_out24[5]),
    .out30(demultiplexer_1_out24[6]), .out31(demultiplexer_1_out24[7]), .in(WRITE), .sel(WRITE_REGISTER));
  Register #(.width(32)) register_1 (
    .D(WRITE_DATA), .en(demultiplexer_1_out0[0]), .clk(CLOCK), .Q(register_1_q), .clr(1'b1));
  Register #(.width(32)) register_2 (
    .D(WRITE_DATA), .en(demultiplexer_1_out0[1]), .clk(CLOCK), .Q(register_2_q), .clr(1'b0));
  Register #(.width(32)) register_3 (
    .D(WRITE_DATA), .en(demultiplexer_1_out0[2]), .clk(CLOCK), .Q(register_3_q), .clr(1'b0));
  Register #(.width(32)) register_4 (
    .D(WRITE_DATA), .en(demultiplexer_1_out0[3]), .clk(CLOCK), .Q(register_4_q), .clr(1'b0));
  Register #(.width(32)) register_5 (
    .D(WRITE_DATA), .en(demultiplexer_1_out0[4]), .clk(CLOCK), .Q(register_5_q), .clr(1'b0));
  Register #(.width(32)) register_6 (
    .D(WRITE_DATA), .en(demultiplexer_1_out0[5]), .clk(CLOCK), .Q(register_6_q), .clr(1'b0));
  Register #(.width(32)) register_7 (
    .D(WRITE_DATA), .en(demultiplexer_1_out0[6]), .clk(CLOCK), .Q(register_7_q), .clr(1'b0));
  Register #(.width(32)) register_8 (
    .D(WRITE_DATA), .en(demultiplexer_1_out0[7]), .clk(CLOCK), .Q(register_8_q), .clr(1'b0));
  Register #(.width(32)) register_9 (
    .D(WRITE_DATA), .en(demultiplexer_1_out8[0]), .clk(CLOCK), .Q(register_9_q), .clr(1'b0));
  Register #(.width(32)) register_10 (
    .D(WRITE_DATA), .en(demultiplexer_1_out8[1]), .clk(CLOCK), .Q(register_10_q), .clr(1'b0));
  Register #(.width(32)) register_11 (
    .D(WRITE_DATA), .en(demultiplexer_1_out8[2]), .clk(CLOCK), .Q(register_11_q), .clr(1'b0));
  Register #(.width(32)) register_12 (
    .D(WRITE_DATA), .en(demultiplexer_1_out8[3]), .clk(CLOCK), .Q(register_12_q), .clr(1'b0));
  Register #(.width(32)) register_13 (
    .D(WRITE_DATA), .en(demultiplexer_1_out8[4]), .clk(CLOCK), .Q(register_13_q), .clr(1'b0));
  Register #(.width(32)) register_14 (
    .D(WRITE_DATA), .en(demultiplexer_1_out8[5]), .clk(CLOCK), .Q(register_14_q), .clr(1'b0));
  Register #(.width(32)) register_15 (
    .D(WRITE_DATA), .en(demultiplexer_1_out8[6]), .clk(CLOCK), .Q(register_15_q), .clr(1'b0));
  Register #(.width(32)) register_16 (
    .D(WRITE_DATA), .en(demultiplexer_1_out8[7]), .clk(CLOCK), .Q(register_16_q), .clr(1'b0));
  Register #(.width(32)) register_17 (
    .D(WRITE_DATA), .en(demultiplexer_1_out16[0]), .clk(CLOCK), .Q(register_17_q), .clr(1'b0));
  Register #(.width(32)) register_18 (
    .D(WRITE_DATA), .en(demultiplexer_1_out16[1]), .clk(CLOCK), .Q(register_18_q), .clr(1'b0));
  Register #(.width(32)) register_19 (
    .D(WRITE_DATA), .en(demultiplexer_1_out16[2]), .clk(CLOCK), .Q(register_19_q), .clr(1'b0));
  Register #(.width(32)) register_20 (
    .D(WRITE_DATA), .en(demultiplexer_1_out16[3]), .clk(CLOCK), .Q(register_20_q), .clr(1'b0));
  Register #(.width(32)) register_21 (
    .D(WRITE_DATA), .en(demultiplexer_1_out16[4]), .clk(CLOCK), .Q(register_21_q), .clr(1'b0));
  Register #(.width(32)) register_22 (
    .D(WRITE_DATA), .en(demultiplexer_1_out16[5]), .clk(CLOCK), .Q(register_22_q), .clr(1'b0));
  Register #(.width(32)) register_23 (
    .D(WRITE_DATA), .en(demultiplexer_1_out16[6]), .clk(CLOCK), .Q(register_23_q), .clr(1'b0));
  Register #(.width(32)) register_24 (
    .D(WRITE_DATA), .en(demultiplexer_1_out16[7]), .clk(CLOCK), .Q(register_24_q), .clr(1'b0));
  Register #(.width(32)) register_25 (
    .D(WRITE_DATA), .en(demultiplexer_1_out24[0]), .clk(CLOCK), .Q(register_25_q), .clr(1'b0));
  Register #(.width(32)) register_26 (
    .D(WRITE_DATA), .en(demultiplexer_1_out24[1]), .clk(CLOCK), .Q(register_26_q), .clr(1'b0));
  Register #(.width(32)) register_27 (
    .D(WRITE_DATA), .en(demultiplexer_1_out24[2]), .clk(CLOCK), .Q(register_27_q), .clr(1'b0));
  Register #(.width(32)) register_28 (
    .D(WRITE_DATA), .en(demultiplexer_1_out24[3]), .clk(CLOCK), .Q(register_28_q), .clr(1'b0));
  Register #(.width(32)) register_29 (
    .D(WRITE_DATA), .en(demultiplexer_1_out24[4]), .clk(CLOCK), .Q(register_29_q), .clr(1'b0));
  Register #(.width(32)) register_30 (
    .D(WRITE_DATA), .en(demultiplexer_1_out24[5]), .clk(CLOCK), .Q(register_30_q), .clr(1'b0));
  Register #(.width(32)) register_31 (
    .D(WRITE_DATA), .en(demultiplexer_1_out24[6]), .clk(CLOCK), .Q(register_31_q), .clr(1'b0));
  Register #(.width(32)) register_32 (
    .D(WRITE_DATA), .en(demultiplexer_1_out24[7]), .clk(CLOCK), .Q(register_32_q), .clr(1'b0));
  Multiplexer #(.select(5), .width(32), .enable("false")) multiplexer_1 (
    .in0(register_1_q), .in1(register_2_q), .in2(register_3_q), .in3(register_4_q), .in4(register_5_q),
    .in5(register_6_q), .in6(register_7_q), .in7(register_8_q), .in8(register_9_q), .in9(register_10_q),
    .in10(register_11_q), .in11(register_12_q), .in12(register_13_q), .in13(register_14_q),
    .in14(register_15_q), .in15(register_16_q), .in16(register_17_q), .in17(register_18_q),
    .in18(register_19_q), .in19(register_20_q), .in20(register_21_q), .in21(register_22_q),
    .in22(register_23_q), .in23(register_24_q), .in24(register_25_q), .in25(register_26_q),
    .in26(register_27_q), .in27(register_28_q), .in28(register_29_q), .in29(register_30_q),
    .in30(register_31_q), .in31(register_32_q), .out(READ_DATA_1), .sel(READ_REGISTER_1));
  Multiplexer #(.select(5), .width(32), .enable("false")) multiplexer_2 (
    .in0(register_1_q), .in1(register_2_q), .in2(register_3_q), .in3(register_4_q), .in4(register_5_q),
    .in5(register_6_q), .in6(register_7_q), .in7(register_8_q), .in8(register_9_q), .in9(register_10_q),
    .in10(register_11_q), .in11(register_12_q), .in12(register_13_q), .in13(register_14_q),
    .in14(register_15_q), .in15(register_16_q), .in16(register_17_q), .in17(register_18_q),
    .in18(register_19_q), .in19(register_20_q), .in20(register_21_q), .in21(register_22_q),
    .in22(register_23_q), .in23(register_24_q), .in24(register_25_q), .in25(register_26_q),
    .in26(register_27_q), .in27(register_28_q), .in28(register_29_q), .in29(register_30_q),
    .in30(register_31_q), .in31(register_32_q), .out(READ_DATA_2), .sel(READ_REGISTER_2));
endmodule

module Trab2_ALU (
  input  [31:0] ALU_n1,
  input  [31:0] ALU_n2,
  input  [3:0] ALU_OPERATION,
  output [31:0] ALU_Result,
  output ZERO
);

  wire comparator_1_eq, or_2_out;
  wire [31:0] adder_1_out, and_1_out, bit_extender_1_out, nor_1_out, or_1_out, subtractor_1_out, xor_1_out;

  Adder #(.width(32)) adder_1 (.a(ALU_n1), .b(ALU_n2), .out(adder_1_out), .cin(1'b0));  // open: cout
  Subtractor #(.width(32)) subtractor_1 (.a(ALU_n1), .b(ALU_n2), .out(subtractor_1_out), .bin(1'b0));  // open: bout
  assign and_1_out = ALU_n1 & ALU_n2;  // AND_Gate and_1, 32 bits wide
  assign or_1_out = ALU_n1 | ALU_n2;  // OR_Gate or_1, 32 bits wide
  assign xor_1_out = ALU_n1 ^ ALU_n2;  // XOR_Gate xor_1, 32 bits wide
  assign nor_1_out = ~(ALU_n1 | ALU_n2);  // NOR_Gate nor_1, 32 bits wide
  Comparator #(.width(32)) comparator_1 (.a(ALU_n1), .b(ALU_n2), .eq(comparator_1_eq));  // open: gt, lt
  assign bit_extender_1_out = {{31{comparator_1_eq}}, comparator_1_eq};  // Bit_Extender bit_extender_1
  Multiplexer #(.select(4), .width(32), .enable("false")) multiplexer_1 (
    .in0(adder_1_out), .in1(adder_1_out), .in2(subtractor_1_out), .in3(subtractor_1_out), .in4(and_1_out),
    .in5(or_1_out), .in6(xor_1_out), .in7(nor_1_out), .in8(bit_extender_1_out), .in15(32'h1),
    .out(ALU_Result), .sel(ALU_OPERATION));  // open: in9, in10, in11, in12, in13, in14
  or or_2 (or_2_out, ALU_Result[0], ALU_Result[1], ALU_Result[2], ALU_Result[3], ALU_Result[4], ALU_Result[5], ALU_Result[6], ALU_Result[7], ALU_Result[8], ALU_Result[9], ALU_Result[10], ALU_Result[11], ALU_Result[12], ALU_Result[13], ALU_Result[14], ALU_Result[15], ALU_Result[16], ALU_Result[17], ALU_Result[18], ALU_Result[19], ALU_Result[20], ALU_Result[21], ALU_Result[22], ALU_Result[23], ALU_Result[24], ALU_Result[25], ALU_Result[26], ALU_Result[27], ALU_Result[28], ALU_Result[29], ALU_Result[30], ALU_Result[31]);
  not not_1 (ZERO, or_2_out);
endmodule

module Trab3_SignExtend (
  input  [15:0] In16,
  output [31:0] Out32
);


  assign Out32 = {{17{In16[15]}}, In16[14:0]};
endmodule

module Trab3_DataMemory (
  input  [31:0] Adress,
  input  [31:0] Write_Data,
  input  Mem_Write,
  input  [1:0] WHB,
  input  Mem_Read,
  output [31:0] Read_Data
);

  wire [1:0] demultiplexer_3_out0, demultiplexer_3_out1;
  wire [3:0] demultiplexer_4_out0, multiplexer_1_out;
  wire [7:0] demultiplexer_2_out0, demultiplexer_2_out1, demultiplexer_2_out2, demultiplexer_2_out3,
       multiplexer_4_out, ram_2_dout, ram_3_dout;
  wire [15:0] demultiplexer_1_out0, demultiplexer_1_out1, multiplexer_3_out;
  wire [31:0] multiplexer_2_out, ram_1_dout;

  Demultiplexer #(.width(16), .enable("false")) demultiplexer_1 (
    .out0(demultiplexer_1_out0), .out1(demultiplexer_1_out1), .in(Write_Data[15:0]), .sel(Adress[1]));
  Demultiplexer #(.select(2), .width(8), .enable("false")) demultiplexer_2 (
    .out0(demultiplexer_2_out0), .out1(demultiplexer_2_out1), .out2(demultiplexer_2_out2),
    .out3(demultiplexer_2_out3), .in(Write_Data[7:0]), .sel(Adress[1:0]));
  Demultiplexer #(.width(2), .enable("false")) demultiplexer_3 (
    .out0(demultiplexer_3_out0), .out1(demultiplexer_3_out1), .in({2{Mem_Write}}), .sel(Adress[1]));
  Demultiplexer #(.select(2), .enable("false")) demultiplexer_4 (
    .out0(demultiplexer_4_out0[0]), .out1(demultiplexer_4_out0[1]), .out2(demultiplexer_4_out0[2]),
    .out3(demultiplexer_4_out0[3]), .in(Mem_Write), .sel(Adress[1:0]));
  Multiplexer #(.select(2), .width(4), .enable("false")) multiplexer_1 (
    .in0({4{Mem_Write}}), .in1({demultiplexer_3_out1, demultiplexer_3_out0}), .in2(demultiplexer_4_out0),
    .out(multiplexer_1_out), .sel(WHB));  // open: in3
  Multiplexer #(.select(2), .width(32), .enable("false")) multiplexer_2 (
    .in0(Write_Data), .in1({demultiplexer_1_out1, demultiplexer_1_out0}),
    .in2({demultiplexer_2_out3, demultiplexer_2_out2, demultiplexer_2_out1, demultiplexer_2_out0}),
    .out(multiplexer_2_out), .sel(WHB));  // open: in3
  RAM #(.addrWidth(24), .trigger("high"), .databus("bibus")) ram_1 (
    .addr(Adress[25:2]), .we(multiplexer_1_out[0]), .oe(Mem_Read), .din(multiplexer_2_out[7:0]),
    .dout(ram_1_dout[7:0]));
  RAM #(.addrWidth(24), .trigger("high"), .databus("bibus")) ram_2 (
    .addr(Adress[25:2]), .we(multiplexer_1_out[1]), .oe(Mem_Read), .din(multiplexer_2_out[15:8]),
    .dout(ram_2_dout));
  RAM #(.addrWidth(24), .trigger("high"), .databus("bibus")) ram_3 (
    .addr(Adress[25:2]), .we(multiplexer_1_out[2]), .oe(Mem_Read), .din(multiplexer_2_out[23:16]),
    .dout(ram_3_dout));
  RAM #(.addrWidth(24), .trigger("high"), .databus("bibus")) ram_4 (
    .addr(Adress[25:2]), .we(multiplexer_1_out[3]), .oe(Mem_Read), .din(multiplexer_2_out[31:24]),
    .dout(ram_1_dout[31:24]));
  Multiplexer #(.width(16), .enable("false")) multiplexer_3 (
    .in0({ram_2_dout, ram_1_dout[7:0]}), .in1({ram_1_dout[31:24], ram_3_dout}), .out(multiplexer_3_out),
    .sel(Adress[1]));
  Multiplexer #(.select(2), .width(8), .enable("false")) multiplexer_4 (
    .in0(ram_1_dout[7:0]), .in1(ram_2_dout), .in2(ram_3_dout), .in3(ram_1_dout[31:24]),
    .out(multiplexer_4_out), .sel(Adress[1:0]));
  Multiplexer #(.select(2), .width(32), .enable("false")) multiplexer_5 (
    .in0({ram_1_dout[31:24], ram_3_dout, ram_2_dout, ram_1_dout[7:0]}),
    .in1({{16{1'b0}}, multiplexer_3_out}), .in2({{24{1'b0}}, multiplexer_4_out}), .out(Read_Data), .sel(WHB));  // open: in3

  // Other names for the same wires on the sheet: A0A1[1:0] = Adress[1:0]; A1 = Adress[1]

  // Notes on the sheet:
  //   00 Word  /  01 Half  / 10 Bit
endmodule

module Trab3 (
  input  Clock,
  input  WE,
  input  PCReset
);

  wire ALUSrc, and_1_out, Branch, Jal, Jump, JumpRegister, MemRead, MemtoReg, MemWrite, RegDst, RegWrite,
       trab2_alu_1_zero;
  wire [1:0] WHB;
  wire [2:0] ALUOp;
  wire [3:0] trab4_alucontrol_1_alucode;
  wire [4:0] multiplexer_1_out, multiplexer_2_out;
  wire [31:0] adder_1_out, adder_2_out, multiplexer_3_out, multiplexer_4_out, multiplexer_5_out,
       multiplexer_6_out, multiplexer_7_out, multiplexer_8_out, shifter_1_out, trab1_1_instruction,
       trab1_1_read_adress_out, trab2_alu_1_alu_result, trab2_registers_1_read_data_1,
       trab2_registers_1_read_data_2, trab3_datamemory_1_read_data, trab3_signextend_1_out32,
       trab5_instruction_compose_1_target;

  Trab4_Control trab4_control_1 (
    .Instruction_IN(trab1_1_instruction[31:26]), .RegDst(RegDst), .Branch(Branch), .MemRead(MemRead),
    .MemtoReg(MemtoReg), .ALUOp(ALUOp), .MemWrite(MemWrite), .ALUSrc(ALUSrc), .RegWrite(RegWrite), .WHB(WHB),
    .Jump(Jump), .Jal(Jal));
  Trab1 trab1_1 (
    .Read_Adress_In(multiplexer_3_out), .WE(WE), .Clk(Clock), .RESET(PCReset),
    .Read_Adress_Out(trab1_1_read_adress_out), .Instruction(trab1_1_instruction));
  Multiplexer #(.width(5), .enable("false")) multiplexer_1 (
    .in0(trab1_1_instruction[20:16]), .in1(trab1_1_instruction[15:11]), .out(multiplexer_1_out), .sel(RegDst));
  Multiplexer #(.width(5), .enable("false")) multiplexer_2 (
    .in0(multiplexer_1_out), .in1({5{1'b1}}), .out(multiplexer_2_out), .sel(Jal));
  Adder #(.width(32)) adder_1 (.a(trab1_1_read_adress_out), .b(32'h4), .out(adder_1_out), .cin(1'b0));  // open: cout
  Multiplexer #(.width(32), .enable("false")) multiplexer_3 (
    .in0(multiplexer_6_out), .in1(trab2_registers_1_read_data_1), .out(multiplexer_3_out), .sel(JumpRegister));
  Trab5_Instruction_Compose trab5_instruction_compose_1 (
    .Instruction(trab1_1_instruction), .PC(adder_1_out), .Target(trab5_instruction_compose_1_target));
  Trab2_Registers trab2_registers_1 (
    .READ_REGISTER_1(trab1_1_instruction[25:21]), .READ_REGISTER_2(trab1_1_instruction[20:16]),
    .WRITE_REGISTER(multiplexer_2_out), .WRITE_DATA(multiplexer_8_out), .WRITE(RegWrite), .CLOCK(Clock),
    .READ_DATA_1(trab2_registers_1_read_data_1), .READ_DATA_2(trab2_registers_1_read_data_2));
  Trab3_SignExtend trab3_signextend_1 (.In16(trab1_1_instruction[15:0]), .Out32(trab3_signextend_1_out32));
  Trab4_ALUControl trab4_alucontrol_1 (
    .ALU_Instruction(trab1_1_instruction[5:0]), .ALUOp(ALUOp), .ALUCode(trab4_alucontrol_1_alucode),
    .JumpRegister(JumpRegister));
  Multiplexer #(.width(32), .enable("false")) multiplexer_4 (
    .in0(trab2_registers_1_read_data_2), .in1(trab3_signextend_1_out32), .out(multiplexer_4_out), .sel(ALUSrc));
  Shifter #(.width(32)) shifter_1 (.in(trab3_signextend_1_out32), .\dist (5'b00010), .out(shifter_1_out));
  Adder #(.width(32)) adder_2 (.a(adder_1_out), .b(shifter_1_out), .out(adder_2_out), .cin(1'b0));  // open: cout
  Trab2_ALU trab2_alu_1 (
    .ALU_n1(trab2_registers_1_read_data_1), .ALU_n2(multiplexer_4_out),
    .ALU_OPERATION(trab4_alucontrol_1_alucode), .ALU_Result(trab2_alu_1_alu_result), .ZERO(trab2_alu_1_zero));
  and and_1 (and_1_out, Branch, trab2_alu_1_zero);
  Multiplexer #(.width(32), .enable("false")) multiplexer_5 (
    .in0(adder_1_out), .in1(adder_2_out), .out(multiplexer_5_out), .sel(and_1_out));
  Multiplexer #(.width(32), .enable("false")) multiplexer_6 (
    .in0(multiplexer_5_out), .in1(trab5_instruction_compose_1_target), .out(multiplexer_6_out), .sel(Jump));
  Trab3_DataMemory trab3_datamemory_1 (
    .Adress(trab2_alu_1_alu_result), .Write_Data(trab2_registers_1_read_data_2), .Mem_Write(MemWrite),
    .WHB(WHB), .Mem_Read(MemRead), .Read_Data(trab3_datamemory_1_read_data));
  Multiplexer #(.width(32), .enable("false")) multiplexer_7 (
    .in0(trab2_alu_1_alu_result), .in1(trab3_datamemory_1_read_data), .out(multiplexer_7_out), .sel(MemtoReg));
  Multiplexer #(.width(32), .enable("false")) multiplexer_8 (
    .in0(multiplexer_7_out), .in1(adder_1_out), .out(multiplexer_8_out), .sel(Jal));
endmodule

module Trab4_Control (
  input  [5:0] Instruction_IN,
  output RegDst,
  output Branch,
  output MemRead,
  output MemtoReg,
  output [2:0] ALUOp,
  output MemWrite,
  output ALUSrc,
  output RegWrite,
  output [1:0] WHB,
  output Jump,
  output Jal
);

  wire [15:14] rom_1_data;

  ROM #(.addrWidth(6), .dataWidth(16)) rom_1 (
    .addr(Instruction_IN),
    .data({rom_1_data, Jal, Jump, WHB, RegWrite, ALUSrc, MemWrite, ALUOp, MemtoReg, MemRead, Branch, RegDst}));

  // Notes on the sheet:
  //   contents of rom_1 (hex, n*v repeats v):
  //   201 0 1010 3210 42 52 0 0 211 211 0 0 221 231 241 17*0 81c 71c 0 31c 81c 71c 0 0 990 590 0 190
  //   00 Word  /  01 Half  / 10 Bit
endmodule

module Trab4_ALUControl (
  input  [5:0] ALU_Instruction,
  input  [2:0] ALUOp,
  output [3:0] ALUCode,
  output JumpRegister
);

  wire comparator_1_eq, comparator_2_eq;

  Multiplexer #(.select(3), .width(4), .enable("false")) multiplexer_1 (
    .in0(ALU_Instruction[3:0]), .in1(4'b0000), .in2(4'b0100), .in3(4'b0101), .in4(4'b0110), .in5(4'b1000),
    .out(ALUCode), .sel(ALUOp));  // open: in6, in7
  Comparator #(.width(6)) comparator_1 (.a(6'b001000), .b(ALU_Instruction), .eq(comparator_1_eq));  // open: gt, lt
  Comparator #(.width(3)) comparator_2 (.a(ALUOp), .b(3'b000), .eq(comparator_2_eq));  // open: gt, lt
  and and_1 (JumpRegister, comparator_2_eq, comparator_1_eq);
endmodule

module Trab5_Instruction_Compose (
  input  [31:0] Instruction,
  input  [31:0] PC,
  output [31:0] Target
);


  assign Target = {PC[31:28], Instruction[25:0], 2'b00};
endmodule
