// Logisim project trab1.circ as structural Verilog: 1 circuit, main circuit main
module main (
  input  clock,
  output [31:0] out_2
);

  wire [31:0] adder_1_out, PC_q;

  Register #(.width(32)) PC (.D(adder_1_out), .en(1'b1), .clk(clock), .Q(PC_q), .clr(1'b0));
  ROM #(.addrWidth(24), .dataWidth(32)) rom_1 (.addr(PC_q[25:2]), .data(out_2));
  Adder #(.width(32)) adder_1 (.a(PC_q), .b(32'h4), .out(adder_1_out), .cin(1'b0));  // open: cout

  // Notes on the sheet:
  //   contents of rom_1 (hex, n*v repeats v):
  //   45645 4d454f4 1564784 122 12*0 aa 15*0 aaaa 28*0 867676 44*0 7687687 16*0 6786876 6*0 a 60*0 7678687
  //   21*0 dad 14*0 a
endmodule
