// Logisim project trabalho3_LeandroFurlam.circ as structural Verilog: 8 circuits, main circuit lab3
module main (
  input  in_1,
  input  in_2,
  input  in_3,
  input  in_4,
  input  [2:0] in_5,
  input  in_6,
  input  in_7,
  input  in_8,
  input  [1:0] in_9,
  input  in_10,
  input  in_11,
  output [31:0] out_12,
  output [31:0] out_13,
  output [4:0] out_14,
  output [4:0] out_15,
  output [31:0] out_16,
  output [31:0] out_17
);

  lab3 lab3_1 (
    .WritePC(in_1), .RegDst(in_2), .RegWrite(in_3), .PCSrc(in_4), .ALUControl(in_5), .ALUSrc(in_6),
    .MemWrite(in_7), .MemRead(in_8), .WHB(in_9), .MemtoReg(in_10), .Clock(in_11), .ALUIn0(out_12),
    .ALUIn1(out_13), .Register_1(out_14), .Register_2(out_15), .ALUOut(out_16), .dataOut(out_17));
endmodule

module lab3 (
  input  WritePC,
  input  RegDst,
  input  RegWrite,
  input  PCSrc,
  input  [2:0] ALUControl,
  input  ALUSrc,
  input  MemWrite,
  input  MemRead,
  input  [1:0] WHB,
  input  MemtoReg,
  input  Clock,
  output [31:0] ALUIn0,
  output [31:0] ALUIn1,
  output [4:0] Register_1,
  output [4:0] Register_2,
  output [31:0] ALUOut,
  output [31:0] dataOut
);

  wire [4:0] multiplexer_1_out;
  wire [31:0] adder_1_out, datamemory_1_data, multiplexer_2_out, pc_1_instruction, pc_1_pcadd4,
       registers_1_register_2, shiftleft2_1_out_0, signextend_1_out_0;

  PC pc_1 (
    .ReadInstruction(multiplexer_2_out), .WritePC(WritePC), .clock(Clock), .PCadd4(pc_1_pcadd4),
    .Instruction({pc_1_instruction[31:26], Register_1, Register_2, pc_1_instruction[15:0]}));
  Multiplexer #(.width(5), .enable("false")) multiplexer_1 (
    .in0(Register_2), .in1(pc_1_instruction[15:11]), .out(multiplexer_1_out), .sel(RegDst));
  signExtend signextend_1 (.In_0(pc_1_instruction[15:0]), .Out_0(signextend_1_out_0));
  shiftLeft2 shiftleft2_1 (.In_0(signextend_1_out_0), .Out_0(shiftleft2_1_out_0));
  Multiplexer #(.width(32), .enable("false")) multiplexer_2 (
    .in0(pc_1_pcadd4), .in1(adder_1_out), .out(multiplexer_2_out), .sel(PCSrc));
  Adder #(.width(32)) adder_1 (.a(pc_1_pcadd4), .b(shiftleft2_1_out_0), .out(adder_1_out), .cin(1'b0));  // open: cout
  registers registers_1 (
    .RegWrite(RegWrite), .Data(dataOut), .WriteRegister(multiplexer_1_out), .ReadRegister_1(Register_1),
    .ReadRegister_2(Register_2), .Clock(Clock), .Register_1(ALUIn0), .Register_2(registers_1_register_2));
  Multiplexer #(.width(32), .enable("false")) multiplexer_3 (
    .in0(registers_1_register_2), .in1(signextend_1_out_0), .out(ALUIn1), .sel(ALUSrc));
  ALU alu_1 (.In0(ALUIn0), .In1(ALUIn1), .ALUControl(ALUControl), .ALUOut(ALUOut));  // open: Zero
  dataMemory datamemory_1 (
    .WHB(WHB), .MemoryRead(MemRead), .Adress(ALUOut), .MemoryWrite(MemWrite),
    .WriteData(registers_1_register_2), .Clock(Clock), .Data(datamemory_1_data));
  Multiplexer #(.width(32), .enable("false")) multiplexer_4 (
    .in0(ALUOut), .in1(datamemory_1_data), .out(dataOut), .sel(MemtoReg));
endmodule

module PC (
  input  [31:0] ReadInstruction,
  input  WritePC,
  input  clock,
  output [31:0] PCadd4,
  output [31:0] Instruction
);

  wire [31:0] register_1_q;

  Register #(.width(32)) register_1 (.D(ReadInstruction), .en(WritePC), .clk(clock), .Q(register_1_q), .clr(1'b0));
  ROM #(.addrWidth(24), .dataWidth(32)) rom_1 (.addr(register_1_q[25:2]), .data(Instruction));
  Adder #(.width(32)) adder_1 (.a(register_1_q), .b(32'h4), .out(PCadd4), .cin(1'b0));  // open: cout

  // Notes on the sheet:
  //   contents of rom_1 (hex, n*v repeats v):
  //   21210000
endmodule

module registers (
  input  RegWrite,
  input  [31:0] Data,
  input  [4:0] WriteRegister,
  input  [4:0] ReadRegister_1,
  input  [4:0] ReadRegister_2,
  input  Clock,
  output [31:0] Register_1,
  output [31:0] Register_2
);

  wire demultiplexer_1_out0, demultiplexer_1_out1, demultiplexer_1_out2, demultiplexer_1_out3,
       demultiplexer_1_out4, demultiplexer_1_out5, demultiplexer_1_out6, demultiplexer_1_out7,
       demultiplexer_1_out8, demultiplexer_1_out9, demultiplexer_1_out10, demultiplexer_1_out11,
       demultiplexer_1_out12, demultiplexer_1_out13, demultiplexer_1_out14, demultiplexer_1_out15,
       demultiplexer_1_out16, demultiplexer_1_out17, demultiplexer_1_out18, demultiplexer_1_out19,
       demultiplexer_1_out20, demultiplexer_1_out21, demultiplexer_1_out22, demultiplexer_1_out23,
       demultiplexer_1_out24, demultiplexer_1_out25, demultiplexer_1_out26, demultiplexer_1_out27,
       demultiplexer_1_out28, demultiplexer_1_out29, demultiplexer_1_out30, demultiplexer_1_out31;
  wire [31:0] register_1_q, register_2_q, register_3_q, register_4_q, register_5_q, register_6_q,
       register_7_q, register_8_q, register_9_q, register_10_q, register_11_q, register_12_q, register_13_q,
       register_14_q, register_15_q, register_16_q, register_17_q, register_18_q, register_19_q,
       register_20_q, register_21_q, register_22_q, register_23_q, register_24_q, register_25_q,
       register_26_q, register_27_q, register_28_q, register_29_q, register_30_q, register_31_q,
       register_32_q;

  Demultiplexer #(.select(5), .enable("false")) demultiplexer_1 (
    .out0(demultiplexer_1_out0), .out1(demultiplexer_1_out1), .out2(demultiplexer_1_out2),
    .out3(demultiplexer_1_out3), .out4(demultiplexer_1_out4), .out5(demultiplexer_1_out5),
    .out6(demultiplexer_1_out6), .out7(demultiplexer_1_out7), .out8(demultiplexer_1_out8),
    .out9(demultiplexer_1_out9), .out10(demultiplexer_1_out10), .out11(demultiplexer_1_out11),
    .out12(demultiplexer_1_out12), .out13(demultiplexer_1_out13), .out14(demultiplexer_1_out14),
    .out15(demultiplexer_1_out15), .out16(demultiplexer_1_out16), .out17(demultiplexer_1_out17),
    .out18(demultiplexer_1_out18), .out19(demultiplexer_1_out19), .out20(demultiplexer_1_out20),
    .out21(demultiplexer_1_out21), .out22(demultiplexer_1_out22), .out23(demultiplexer_1_out23),
    .out24(demultiplexer_1_out24), .out25(demultiplexer_1_out25), .out26(demultiplexer_1_out26),
    .out27(demultiplexer_1_out27), .out28(demultiplexer_1_out28), .out29(demultiplexer_1_out29),
    .out30(demultiplexer_1_out30), .out31(demultiplexer_1_out31), .in(RegWrite), .sel(WriteRegister));
  Register #(.width(32)) u_register_1 (.D(Data), .en(demultiplexer_1_out0), .clk(Clock), .Q(register_1_q), .clr(1'b1));
  Register #(.width(32)) u_register_2 (.D(Data), .en(demultiplexer_1_out4), .clk(Clock), .Q(register_2_q), .clr(1'b0));
  Register #(.width(32)) register_3 (.D(Data), .en(demultiplexer_1_out8), .clk(Clock), .Q(register_3_q), .clr(1'b0));
  Register #(.width(32)) register_4 (.D(Data), .en(demultiplexer_1_out12), .clk(Clock), .Q(register_4_q), .clr(1'b0));
  Register #(.width(32)) register_5 (.D(Data), .en(demultiplexer_1_out16), .clk(Clock), .Q(register_5_q), .clr(1'b0));
  Register #(.width(32)) register_6 (.D(Data), .en(demultiplexer_1_out20), .clk(Clock), .Q(register_6_q), .clr(1'b0));
  Register #(.width(32)) register_7 (.D(Data), .en(demultiplexer_1_out24), .clk(Clock), .Q(register_7_q), .clr(1'b0));
  Register #(.width(32)) register_8 (.D(Data), .en(demultiplexer_1_out28), .clk(Clock), .Q(register_8_q), .clr(1'b0));
  Register #(.width(32)) register_9 (.D(Data), .en(demultiplexer_1_out1), .clk(Clock), .Q(register_9_q), .clr(1'b0));
  Register #(.width(32)) register_10 (.D(Data), .en(demultiplexer_1_out5), .clk(Clock), .Q(register_10_q), .clr(1'b0));
  Register #(.width(32)) register_11 (.D(Data), .en(demultiplexer_1_out9), .clk(Clock), .Q(register_11_q), .clr(1'b0));
  Register #(.width(32)) register_12 (.D(Data), .en(demultiplexer_1_out13), .clk(Clock), .Q(register_12_q), .clr(1'b0));
  Register #(.width(32)) register_13 (.D(Data), .en(demultiplexer_1_out17), .clk(Clock), .Q(register_13_q), .clr(1'b0));
  Register #(.width(32)) register_14 (.D(Data), .en(demultiplexer_1_out21), .clk(Clock), .Q(register_14_q), .clr(1'b0));
  Register #(.width(32)) register_15 (.D(Data), .en(demultiplexer_1_out25), .clk(Clock), .Q(register_15_q), .clr(1'b0));
  Register #(.width(32)) register_16 (.D(Data), .en(demultiplexer_1_out29), .clk(Clock), .Q(register_16_q), .clr(1'b0));
  Register #(.width(32)) register_17 (.D(Data), .en(demultiplexer_1_out2), .clk(Clock), .Q(register_17_q), .clr(1'b0));
  Register #(.width(32)) register_18 (.D(Data), .en(demultiplexer_1_out6), .clk(Clock), .Q(register_18_q), .clr(1'b0));
  Register #(.width(32)) register_19 (.D(Data), .en(demultiplexer_1_out10), .clk(Clock), .Q(register_19_q), .clr(1'b0));
  Register #(.width(32)) register_20 (.D(Data), .en(demultiplexer_1_out14), .clk(Clock), .Q(register_20_q), .clr(1'b0));
  Register #(.width(32)) register_21 (.D(Data), .en(demultiplexer_1_out18), .clk(Clock), .Q(register_21_q), .clr(1'b0));
  Register #(.width(32)) register_22 (.D(Data), .en(demultiplexer_1_out22), .clk(Clock), .Q(register_22_q), .clr(1'b0));
  Register #(.width(32)) register_23 (.D(Data), .en(demultiplexer_1_out26), .clk(Clock), .Q(register_23_q), .clr(1'b0));
  Register #(.width(32)) register_24 (.D(Data), .en(demultiplexer_1_out30), .clk(Clock), .Q(register_24_q), .clr(1'b0));
  Register #(.width(32)) register_25 (.D(Data), .en(demultiplexer_1_out3), .clk(Clock), .Q(register_25_q), .clr(1'b0));
  Register #(.width(32)) register_26 (.D(Data), .en(demultiplexer_1_out7), .clk(Clock), .Q(register_26_q), .clr(1'b0));
  Register #(.width(32)) register_27 (.D(Data), .en(demultiplexer_1_out11), .clk(Clock), .Q(register_27_q), .clr(1'b0));
  Register #(.width(32)) register_28 (.D(Data), .en(demultiplexer_1_out15), .clk(Clock), .Q(register_28_q), .clr(1'b0));
  Register #(.width(32)) register_29 (.D(Data), .en(demultiplexer_1_out19), .clk(Clock), .Q(register_29_q), .clr(1'b0));
  Register #(.width(32)) register_30 (.D(Data), .en(demultiplexer_1_out23), .clk(Clock), .Q(register_30_q), .clr(1'b0));
  Register #(.width(32)) register_31 (.D(Data), .en(demultiplexer_1_out27), .clk(Clock), .Q(register_31_q), .clr(1'b0));
  Register #(.width(32)) register_32 (.D(Data), .en(demultiplexer_1_out31), .clk(Clock), .Q(register_32_q), .clr(1'b0));
  Multiplexer #(.select(5), .width(32), .enable("false")) multiplexer_1 (
    .in0(register_1_q), .in1(register_9_q), .in2(register_17_q), .in3(register_25_q), .in4(register_2_q),
    .in5(register_10_q), .in6(register_18_q), .in7(register_26_q), .in8(register_3_q), .in9(register_11_q),
    .in10(register_19_q), .in11(register_27_q), .in12(register_4_q), .in13(register_12_q),
    .in14(register_20_q), .in15(register_28_q), .in16(register_5_q), .in17(register_13_q),
    .in18(register_21_q), .in19(register_29_q), .in20(register_6_q), .in21(register_14_q),
    .in22(register_22_q), .in23(register_30_q), .in24(register_7_q), .in25(register_15_q),
    .in26(register_23_q), .in27(register_31_q), .in28(register_8_q), .in29(register_16_q),
    .in30(register_24_q), .in31(register_32_q), .out(Register_1), .sel(ReadRegister_1));
  Multiplexer #(.select(5), .width(32), .enable("false")) multiplexer_2 (
    .in0(register_1_q), .in1(register_9_q), .in2(register_17_q), .in3(register_25_q), .in4(register_2_q),
    .in5(register_10_q), .in6(register_18_q), .in7(register_26_q), .in8(register_3_q), .in9(register_11_q),
    .in10(register_19_q), .in11(register_27_q), .in12(register_4_q), .in13(register_12_q),
    .in14(register_20_q), .in15(register_28_q), .in16(register_5_q), .in17(register_13_q),
    .in18(register_21_q), .in19(register_29_q), .in20(register_6_q), .in21(register_14_q),
    .in22(register_22_q), .in23(register_30_q), .in24(register_7_q), .in25(register_15_q),
    .in26(register_23_q), .in27(register_31_q), .in28(register_8_q), .in29(register_16_q),
    .in30(register_24_q), .in31(register_32_q), .out(Register_2), .sel(ReadRegister_2));
endmodule

module ALU (
  input  [31:0] In0,
  input  [31:0] In1,
  input  [2:0] ALUControl,
  output [31:0] ALUOut,
  output Zero
);

  wire [31:0] adder_1_out, and_1_out, nor_1_out, or_1_out, subtractor_1_out;

  Adder #(.width(32)) adder_1 (.a(In0), .b(In1), .out(adder_1_out), .cin(1'b0));  // open: cout
  Subtractor #(.width(32)) subtractor_1 (.a(In0), .b(In1), .out(subtractor_1_out), .bin(1'b0));  // open: bout
  assign and_1_out = In0 & In1;  // AND_Gate and_1, 32 bits wide
  assign or_1_out = In0 | In1;  // OR_Gate or_1, 32 bits wide
  assign nor_1_out = ~(In0 | In1);  // NOR_Gate nor_1, 32 bits wide
  Multiplexer #(.select(3), .width(32), .enable("false")) multiplexer_1 (
    .in0(adder_1_out), .in1(subtractor_1_out), .in2(and_1_out), .in3(or_1_out), .in4(nor_1_out),
    .out(ALUOut), .sel(ALUControl));  // open: in5, in6, in7
  nor nor_2 (Zero, ALUOut[0], ALUOut[1], ALUOut[2], ALUOut[3], ALUOut[4], ALUOut[5], ALUOut[6], ALUOut[7], ALUOut[8], ALUOut[9], ALUOut[10], ALUOut[11], ALUOut[12], ALUOut[13], ALUOut[14], ALUOut[15], ALUOut[17], ALUOut[18], ALUOut[19], ALUOut[20], ALUOut[21], ALUOut[22], ALUOut[23], ALUOut[24], ALUOut[25], ALUOut[26], ALUOut[27], ALUOut[28], ALUOut[29], ALUOut[30], ALUOut[31], ALUOut[16]);
endmodule

module signExtend (
  input  [15:0] In_0,
  output [31:0] Out_0
);


  assign Out_0 = {{17{In_0[15]}}, In_0[14:0]};
endmodule

module dataMemory (
  input  [1:0] WHB,
  input  MemoryRead,
  input  [31:0] Adress,
  input  MemoryWrite,
  input  [31:0] WriteData,
  input  Clock,
  output [31:0] Data
);

  wire [1:0] demultiplexer_2_out0, demultiplexer_2_out1;
  wire [3:0] demultiplexer_3_out0, multiplexer_2_out;
  wire [7:0] demultiplexer_4_out0, demultiplexer_4_out1, demultiplexer_4_out2, demultiplexer_4_out3,
       multiplexer_4_out, ram_1_dout, ram_2_dout, ram_3_dout, ram_4_dout;
  wire [15:0] demultiplexer_1_out0, demultiplexer_1_out1, multiplexer_3_out;
  wire [31:0] multiplexer_1_out;

  Demultiplexer #(.width(16), .enable("false")) demultiplexer_1 (
    .out0(demultiplexer_1_out0), .out1(demultiplexer_1_out1), .in(WriteData[15:0]), .sel(Adress[1]));
  Demultiplexer #(.width(2), .enable("false")) demultiplexer_2 (
    .out0(demultiplexer_2_out0), .out1(demultiplexer_2_out1), .in({2{MemoryWrite}}), .sel(Adress[1]));
  Demultiplexer #(.select(2), .enable("false")) demultiplexer_3 (
    .out0(demultiplexer_3_out0[0]), .out1(demultiplexer_3_out0[1]), .out2(demultiplexer_3_out0[2]),
    .out3(demultiplexer_3_out0[3]), .in(MemoryWrite), .sel({2{Adress[1]}}));
  Demultiplexer #(.select(2), .width(8), .enable("false")) demultiplexer_4 (
    .out0(demultiplexer_4_out0), .out1(demultiplexer_4_out1), .out2(demultiplexer_4_out2),
    .out3(demultiplexer_4_out3), .in(WriteData[7:0]), .sel({2{Adress[1]}}));
  Multiplexer #(.select(2), .width(32), .enable("false")) multiplexer_1 (
    .in0(WriteData), .in1({demultiplexer_1_out1, demultiplexer_1_out0}),
    .in2({demultiplexer_4_out3, demultiplexer_4_out2, demultiplexer_4_out1, demultiplexer_4_out0}),
    .in3({32{1'b0}}), .out(multiplexer_1_out), .sel(WHB));
  Multiplexer #(.select(2), .width(4), .enable("false")) multiplexer_2 (
    .in0({4{MemoryWrite}}), .in1({demultiplexer_2_out1, demultiplexer_2_out0}), .in2(demultiplexer_3_out0),
    .in3(4'b0000), .out(multiplexer_2_out), .sel(WHB));
  RAM #(.addrWidth(24), .trigger("falling"), .databus("bibus")) ram_1 (
    .addr(Adress[25:2]), .we(multiplexer_2_out[0]), .oe(MemoryRead), .clk(Clock),
    .din(multiplexer_1_out[7:0]), .dout(ram_1_dout));
  RAM #(.addrWidth(24), .trigger("falling"), .databus("bibus")) ram_2 (
    .addr(Adress[25:2]), .we(multiplexer_2_out[1]), .oe(MemoryRead), .clk(Clock),
    .din(multiplexer_1_out[15:8]), .dout(ram_2_dout));
  RAM #(.addrWidth(24), .trigger("falling"), .databus("bibus")) ram_3 (
    .addr(Adress[25:2]), .we(multiplexer_2_out[2]), .oe(MemoryRead), .clk(Clock),
    .din(multiplexer_1_out[23:16]), .dout(ram_3_dout));
  RAM #(.addrWidth(24), .trigger("falling"), .databus("bibus")) ram_4 (
    .addr(Adress[25:2]), .we(multiplexer_2_out[3]), .oe(MemoryRead), .clk(Clock),
    .din(multiplexer_1_out[31:24]), .dout(ram_4_dout));
  Multiplexer #(.width(16), .enable("false")) multiplexer_3 (
    .in0({ram_2_dout, ram_1_dout}), .in1({ram_4_dout, ram_3_dout}), .out(multiplexer_3_out), .sel(Adress[1]));
  Multiplexer #(.select(2), .width(8), .enable("false")) multiplexer_4 (
    .in0(ram_1_dout), .in1(ram_2_dout), .in2(ram_3_dout), .in3(ram_4_dout), .out(multiplexer_4_out),
    .sel({2{Adress[1]}}));
  Multiplexer #(.select(2), .width(32), .enable("false")) multiplexer_5 (
    .in0({ram_4_dout, ram_3_dout, ram_2_dout, ram_1_dout}), .in1({{16{1'b0}}, multiplexer_3_out}),
    .in2({{24{1'b0}}, multiplexer_4_out}), .in3({32{1'b0}}), .out(Data), .sel(WHB));

  assign Adress[0] = Adress[1];
endmodule

module shiftLeft2 (
  input  [31:0] In_0,
  output [31:0] Out_0
);


  assign Out_0 = {In_0[29:0], 2'b00};
endmodule
