// Logisim project arqcomp.circ as structural Verilog: 3 circuits, main circuit main
module main (
  input  clock,
  output [31:0] out_2
);

  wire [31:0] adder_1_out, PC_q;

  Register #(.width(32)) PC (.D(adder_1_out), .en(1'b1), .clk(clock), .Q(PC_q), .clr(1'b0));
  ROM #(.addrWidth(24), .dataWidth(32)) rom_1 (.addr(PC_q[25:2]), .data(out_2));
  Adder #(.width(32)) adder_1 (.a(PC_q), .b(32'h4), .out(adder_1_out), .cin(1'b0));  // open: cout

  // Notes on the sheet:
  //   contents of rom_1 (hex, n*v repeats v):
  //   52151 12fda02 ade55add
endmodule

module MUX2x1 (
  input  in0,
  input  in1,
  input  sel,
  output mux_out
);

  wire and_1_out, and_2_out, not_1_out;

  not not_1 (not_1_out, sel);
  and and_1 (and_1_out, in0, not_1_out);
  and and_2 (and_2_out, in1, sel);
  or or_1 (mux_out, and_1_out, and_2_out);
endmodule

module MUX4x1 (
  input  in00,
  input  in01,
  input  in10,
  input  in11,
  input  sel0,
  input  sel1,
  output mux_out
);

  wire mux2x1_1_mux_out, mux2x1_2_mux_out;

  MUX2x1 mux2x1_1 (.in0(in00), .in1(in01), .sel(sel0), .mux_out(mux2x1_1_mux_out));
  MUX2x1 mux2x1_2 (.in0(in10), .in1(in11), .sel(sel0), .mux_out(mux2x1_2_mux_out));
  MUX2x1 mux2x1_3 (.in0(mux2x1_1_mux_out), .in1(mux2x1_2_mux_out), .sel(sel1), .mux_out(mux_out));
endmodule
