// Logisim project arqcomp3.circ as structural Verilog
module SignExt (
  input  [15:0] in_1,
  output [31:0] out_2
);


  assign out_2 = {{17{in_1[15]}}, in_1[14:0]};
endmodule

module DataMem (
  input  [31:0] in_1,
  input  [1:0] in_2
);

  wire undriven_2;
  wire [7:0] ram_1_dout, ram_2_dout, ram_3_dout, ram_4_dout;
  wire [15:0] multiplexer_1_out;
  wire [25:2] undriven;
  wire [31:0] multiplexer_2_out;

  RAM #(.addrWidth(24), .trigger("falling"), .databus("bibus")) ram_1 (
    .addr(undriven), .dout(ram_1_dout));  // open: we, oe, clk, din
  RAM #(.addrWidth(24), .trigger("falling"), .databus("bibus")) ram_2 (
    .addr(undriven), .dout(ram_2_dout));  // open: we, oe, clk, din
  RAM #(.addrWidth(24), .trigger("falling"), .databus("bibus")) ram_3 (
    .addr(undriven), .dout(ram_3_dout));  // open: we, oe, clk, din
  RAM #(.addrWidth(24), .trigger("falling"), .databus("bibus")) ram_4 (
    .addr(undriven), .dout(ram_4_dout));  // open: we, oe, clk, din
  Multiplexer #(.width(16), .enable("false")) multiplexer_1 (
    .in0({ram_2_dout, ram_1_dout}), .in1({ram_4_dout, ram_3_dout}), .out(multiplexer_1_out), .sel(undriven_2));
  Multiplexer #(.select(2), .width(32), .enable("false")) multiplexer_2 (
    .in0({ram_4_dout, ram_3_dout, ram_2_dout, ram_1_dout}), .in1({{16{1'b0}}, multiplexer_1_out}),
    .out(multiplexer_2_out), .sel(in_2));  // open: in2, in3
endmodule
